// Logisim project Cache.circ as structural Verilog: 5 circuits, main circuit main
module main (
  input  in_1,
  input  [7:0] Fetched_Instruction,
  input  [7:0] Data,
  output [15:0] PC_Address,
  output [15:0] Mem_Address
);

  wire [7:0] decode_1_out_2, decode_2_out_2, decode_4_out_2, register_1_q, register_2_q, register_3_q,
       register_4_q;

  Counter #(.width(16), .max('hffff)) PC (
    .Q(PC_Address), .clk(in_1));  // open: load, D, count, carry, clr, preset, down
  Register #(.Select("low")) register_1 (.D(Fetched_Instruction), .Q(register_1_q), .clk(in_1));  // open: en, clr
  Decode decode_1 (.in_1(register_1_q), .out_2(decode_1_out_2));
  Register #(.Select("low")) register_2 (.D(decode_1_out_2), .Q(register_2_q), .clk(in_1));  // open: en, clr
  Decode decode_2 (.in_1(register_2_q), .out_2(decode_2_out_2));
  Register #(.Select("low")) register_3 (.D(decode_2_out_2), .Q(register_3_q), .clk(in_1));  // open: en, clr
  Decode decode_3 (.in_1(register_3_q), .out_2(Mem_Address[7:0]));
  Register #(.Select("low")) register_4 (.D(Data), .Q(register_4_q), .clk(in_1));  // open: en, clr
  Decode decode_4 (.in_1(register_4_q), .out_2(decode_4_out_2));
  Register #(.Select("low")) register_5 (.D(decode_4_out_2), .clk(in_1));  // open: en, Q, clr

  assign Mem_Address[15:8] = {8{1'b0}};

  // Other names for the same wires on the sheet: clk = in_1
endmodule

module Decode (
  input  [7:0] in_1,
  output [7:0] out_2
);

  Multiplier multiplier_1 (.a(in_1), .b(8'h2), .out(out_2));  // open: cin, cout
endmodule

module RAM (
  input  [15:0] MP_Addr,
  input  [7:0] in_2,
  input  in_3,
  input  in_4,
  input  in_5,
  output [7:0] MP_DataOut
);

  RAM_part #(.addrWidth(16), .bus("separate"), .Select("low")) ram_1 (
    .addr(MP_Addr), .din(in_2), .data(MP_DataOut), .str(in_4), .sel(1'b0), .clk(in_5), .ld(in_3));  // open: clr

  // Other names for the same wires on the sheet: clk = in_5; MP_Ld = in_3; MP_Str = in_4

  // Notes on the sheet:
  //   MP_DataIn
endmodule

module MAIN (
  input  in_1,
  input  [7:0] Fetched_Instruction,
  input  [7:0] Data,
  input  in_4,
  input  [15:0] in_5,
  input  in_6,
  input  in_7,
  input  in_8,
  input  in_9,
  input  [31:0] in_10,
  input  [31:0] in_11,
  input  [31:0] in_12,
  input  [31:0] in_13,
  input  [31:0] in_14,
  input  [31:0] in_15,
  input  [31:0] in_16,
  input  [31:0] in_17,
  input  [15:0] MP_Addr,
  input  [7:0] in_19,
  input  in_20,
  input  in_21,
  input  in_22,
  output [15:0] PC_Address,
  output [15:0] Mem_Address,
  output [7:0] L2_SelectedByte_7__0,
  output out_26,
  output out_27,
  output [7:0] MP_DataOut
);

  wire comparator_1_eq, L2_Tag_RAM_data, L2_Valid_RAM_data;
  wire [7:0] decode_1_out_2, decode_2_out_2, decode_4_out_2, register_1_q, register_2_q, register_3_q,
       register_4_q;
  wire [31:0] L2_DataOut_0_31__0, L2_DataOut_1_31__0, L2_DataOut_2_31__0, L2_DataOut_3_31__0,
       L2_DataOut_4_31__0, L2_DataOut_5_31__0, L2_DataOut_6_31__0, L2_DataOut_7_31__0, multiplexer_1_out,
       multiplexer_2_out;

  main main_1 (.in_1(in_1));  // open: Fetched_Instruction, Data, PC_Address, Mem_Address
  RAM ram_1 ();  // open: in_2, MP_Addr, in_5, in_3, in_4, MP_DataOut
  L2 l2_1 (.in_1(in_1));  // open: in_2, in_3, in_4, in_5, in_6, in_14, in_11, in_12, in_13, in_7, in_8, in_9, in_10, L2_SelectedByte_7__0, out_16, out_17
  Counter #(.width(16), .max('hffff)) PC (
    .Q(PC_Address), .clk(in_1));  // open: load, D, count, carry, clr, preset, down
  Register #(.Select("low")) register_1 (.D(Fetched_Instruction), .Q(register_1_q), .clk(in_1));  // open: en, clr
  Decode decode_1 (.in_1(register_1_q), .out_2(decode_1_out_2));
  RAM_part #(.addrWidth(16), .bus("separate"), .Select("low")) ram_2 (
    .addr(MP_Addr), .din(in_19), .data(MP_DataOut), .str(in_21), .sel(1'b0), .clk(in_1), .ld(in_20));  // open: clr
  Register #(.Select("low")) register_2 (.D(decode_1_out_2), .Q(register_2_q), .clk(in_1));  // open: en, clr
  Decode decode_2 (.in_1(register_2_q), .out_2(decode_2_out_2));
  Register #(.Select("low")) register_3 (.D(decode_2_out_2), .Q(register_3_q), .clk(in_1));  // open: en, clr
  RAM_part #(.addrWidth(10), .dataWidth(1), .bus("separate"), .Select("low")) L2_Tag_RAM (
    .addr(in_5[14:5]), .din(in_5[15]), .data(L2_Tag_RAM_data), .str(in_6), .sel(1'b0), .clk(in_1), .ld(1'b1));  // open: clr
  Decode decode_3 (.in_1(register_3_q), .out_2(Mem_Address[7:0]));
  Multiplexer #(.select(2), .width(32), .enable("false")) multiplexer_1 (
    .in0(L2_DataOut_0_31__0), .in1(L2_DataOut_2_31__0), .in2(L2_DataOut_4_31__0), .in3(L2_DataOut_6_31__0),
    .out(multiplexer_1_out), .sel(in_5[4:3]));
  Multiplexer #(.select(2), .width(32), .enable("false")) multiplexer_2 (
    .in0(L2_DataOut_1_31__0), .in1(L2_DataOut_3_31__0), .in3(L2_DataOut_5_31__0), .out(multiplexer_2_out),
    .sel(in_5[4:3]));  // open: in2
  Comparator #(.width(1)) comparator_1 (.a(L2_Tag_RAM_data), .b(in_5[15]), .eq(comparator_1_eq));  // open: gt, lt
  Register #(.Select("low")) register_4 (.D(Data), .Q(register_4_q), .clk(in_1));  // open: en, clr
  Multiplexer #(.select(3), .width(8), .enable("false")) multiplexer_3 (
    .in0(multiplexer_1_out[7:0]), .in1(multiplexer_1_out[15:8]), .in2(multiplexer_1_out[23:16]),
    .in3(multiplexer_1_out[31:24]), .in4(multiplexer_2_out[7:0]), .in5(multiplexer_2_out[15:8]),
    .in6(multiplexer_2_out[23:16]), .in7(multiplexer_2_out[31:24]), .out(L2_SelectedByte_7__0),
    .sel(in_5[2:0]));
  RAM_part #(.addrWidth(10), .dataWidth(1), .bus("separate"), .Select("low")) L2_Valid_RAM (
    .addr(in_5[14:5]), .din(1'b1), .data(L2_Valid_RAM_data), .str(in_7), .sel(1'b0), .clk(in_1), .ld(1'b1));  // open: clr
  Decode decode_4 (.in_1(register_4_q), .out_2(decode_4_out_2));
  Register #(.Select("low")) register_5 (.D(decode_4_out_2), .clk(in_1));  // open: en, Q, clr
  and and_1 (out_26, L2_Valid_RAM_data, comparator_1_eq);
  not not_1 (out_27, out_26);
  RAM_part #(.addrWidth(10), .dataWidth(32), .bus("separate"), .Select("low")) L2_Data_RAM_0 (
    .addr(in_5[14:5]), .din(in_10), .data(L2_DataOut_0_31__0), .str(in_8), .sel(1'b0), .clk(in_1), .ld(1'b1),
    .clr(in_9));
  RAM_part #(.addrWidth(10), .dataWidth(32), .bus("separate"), .Select("low")) L2_Data_RAM_1 (
    .addr(in_5[14:5]), .din(in_11), .data(L2_DataOut_1_31__0), .str(in_8), .sel(1'b0), .clk(in_1), .ld(1'b1),
    .clr(in_9));
  RAM_part #(.addrWidth(10), .dataWidth(32), .bus("separate"), .Select("low")) L2_Data_RAM_2 (
    .addr(in_5[14:5]), .din(in_12), .data(L2_DataOut_2_31__0), .str(in_8), .sel(1'b0), .clk(in_1), .ld(1'b1),
    .clr(in_9));
  RAM_part #(.addrWidth(10), .dataWidth(32), .bus("separate"), .Select("low")) L2_Data_RAM_3 (
    .addr(in_5[14:5]), .din(in_13), .data(L2_DataOut_3_31__0), .str(in_8), .sel(1'b0), .clk(in_1), .ld(1'b1),
    .clr(in_9));
  RAM_part #(.addrWidth(10), .dataWidth(32), .bus("separate"), .Select("low")) L2_Data_RAM_4 (
    .addr(in_5[14:5]), .din(in_14), .data(L2_DataOut_4_31__0), .str(in_8), .sel(1'b0), .clk(in_1), .ld(1'b1),
    .clr(in_9));
  RAM_part #(.addrWidth(10), .dataWidth(32), .bus("separate"), .Select("low")) L2_Data_RAM_5 (
    .addr(in_5[14:5]), .din(in_15), .data(L2_DataOut_5_31__0), .str(in_8), .sel(1'b0), .clk(in_1), .ld(1'b1),
    .clr(in_9));
  RAM_part #(.addrWidth(10), .dataWidth(32), .bus("separate"), .Select("low")) L2_Data_RAM_6 (
    .addr(in_5[14:5]), .din(in_16), .data(L2_DataOut_6_31__0), .str(in_8), .sel(1'b0), .clk(in_1), .ld(1'b1),
    .clr(in_9));
  RAM_part #(.addrWidth(10), .dataWidth(32), .bus("separate"), .Select("low")) L2_Data_RAM_7 (
    .addr(in_5[14:5]), .din(in_17), .data(L2_DataOut_7_31__0), .str(in_8), .sel(1'b0), .clk(in_1), .ld(1'b1),
    .clr(in_9));

  assign in_4 = in_1;
  assign in_22 = in_1;
  assign Mem_Address[15:8] = {8{1'b0}};

  // Other names for the same wires on the sheet: clk = in_1; L2_Addr[15:0] = in_5; L2_DataIn_0_31__0[31:0] = in_10;
  //   L2_DataIn_1_31__0[31:0] = in_11; L2_DataIn_2_31__0[31:0] = in_12; L2_DataIn_3_31__0[31:0] = in_13;
  //   L2_DataIn_4_31__0[31:0] = in_14; L2_DataIn_5_31__0[31:0] = in_15; L2_DataIn_6_31__0[31:0] = in_16;
  //   L2_DataIn_7_31__0[31:0] = in_17; L2_Hit = out_26; L2_LoadLine = in_9; L2_Miss = out_27; L2_WriteData = in_8;
  //   L2_WriteTag = in_6; L2_WriteValid = in_7; MP_Ld = in_20; MP_Str = in_21

  // Notes on the sheet:
  //   MP_DataIn
  //   L2_Offset
  //   L2_Index
  //   L2_Tag
  //   L2_Tag
  //   L2_StoredTag
  //   L2_TagMatch
  //   L2_Valid
endmodule

module L2 (
  input  in_1,
  input  [15:0] in_2,
  input  in_3,
  input  in_4,
  input  in_5,
  input  in_6,
  input  [31:0] in_7,
  input  [31:0] in_8,
  input  [31:0] in_9,
  input  [31:0] in_10,
  input  [31:0] in_11,
  input  [31:0] in_12,
  input  [31:0] in_13,
  input  [31:0] in_14,
  output [7:0] L2_SelectedByte_7__0,
  output out_16,
  output out_17
);

  wire comparator_1_eq, L2_Tag_RAM_data, L2_Valid_RAM_data;
  wire [31:0] L2_DataOut_0_31__0, L2_DataOut_1_31__0, L2_DataOut_2_31__0, L2_DataOut_3_31__0,
       L2_DataOut_4_31__0, L2_DataOut_5_31__0, L2_DataOut_6_31__0, L2_DataOut_7_31__0, multiplexer_1_out,
       multiplexer_2_out;

  RAM_part #(.addrWidth(10), .dataWidth(1), .bus("separate"), .Select("low")) L2_Tag_RAM (
    .addr(in_2[14:5]), .din(in_2[15]), .data(L2_Tag_RAM_data), .str(in_3), .sel(1'b0), .clk(in_1), .ld(1'b1));  // open: clr
  Comparator #(.width(1)) comparator_1 (.a(L2_Tag_RAM_data), .b(in_2[15]), .eq(comparator_1_eq));  // open: gt, lt
  Multiplexer #(.select(2), .width(32), .enable("false")) multiplexer_1 (
    .in0(L2_DataOut_0_31__0), .in1(L2_DataOut_2_31__0), .in2(L2_DataOut_4_31__0), .in3(L2_DataOut_6_31__0),
    .out(multiplexer_1_out), .sel(in_2[4:3]));
  Multiplexer #(.select(2), .width(32), .enable("false")) multiplexer_2 (
    .in0(L2_DataOut_1_31__0), .in1(L2_DataOut_3_31__0), .in3(L2_DataOut_5_31__0), .out(multiplexer_2_out),
    .sel(in_2[4:3]));  // open: in2
  RAM_part #(.addrWidth(10), .dataWidth(1), .bus("separate"), .Select("low")) L2_Valid_RAM (
    .addr(in_2[14:5]), .din(1'b1), .data(L2_Valid_RAM_data), .str(in_4), .sel(1'b0), .clk(in_1), .ld(1'b1));  // open: clr
  and and_1 (out_16, L2_Valid_RAM_data, comparator_1_eq);
  Multiplexer #(.select(3), .width(8), .enable("false")) multiplexer_3 (
    .in0(multiplexer_1_out[7:0]), .in1(multiplexer_1_out[15:8]), .in2(multiplexer_1_out[23:16]),
    .in3(multiplexer_1_out[31:24]), .in4(multiplexer_2_out[7:0]), .in5(multiplexer_2_out[15:8]),
    .in6(multiplexer_2_out[23:16]), .in7(multiplexer_2_out[31:24]), .out(L2_SelectedByte_7__0),
    .sel(in_2[2:0]));
  not not_1 (out_17, out_16);
  RAM_part #(.addrWidth(10), .dataWidth(32), .bus("separate"), .Select("low")) L2_Data_RAM_0 (
    .addr(in_2[14:5]), .din(in_7), .data(L2_DataOut_0_31__0), .str(in_5), .sel(1'b0), .clk(in_1), .ld(1'b1),
    .clr(in_6));
  RAM_part #(.addrWidth(10), .dataWidth(32), .bus("separate"), .Select("low")) L2_Data_RAM_1 (
    .addr(in_2[14:5]), .din(in_8), .data(L2_DataOut_1_31__0), .str(in_5), .sel(1'b0), .clk(in_1), .ld(1'b1),
    .clr(in_6));
  RAM_part #(.addrWidth(10), .dataWidth(32), .bus("separate"), .Select("low")) L2_Data_RAM_2 (
    .addr(in_2[14:5]), .din(in_9), .data(L2_DataOut_2_31__0), .str(in_5), .sel(1'b0), .clk(in_1), .ld(1'b1),
    .clr(in_6));
  RAM_part #(.addrWidth(10), .dataWidth(32), .bus("separate"), .Select("low")) L2_Data_RAM_3 (
    .addr(in_2[14:5]), .din(in_10), .data(L2_DataOut_3_31__0), .str(in_5), .sel(1'b0), .clk(in_1), .ld(1'b1),
    .clr(in_6));
  RAM_part #(.addrWidth(10), .dataWidth(32), .bus("separate"), .Select("low")) L2_Data_RAM_4 (
    .addr(in_2[14:5]), .din(in_11), .data(L2_DataOut_4_31__0), .str(in_5), .sel(1'b0), .clk(in_1), .ld(1'b1),
    .clr(in_6));
  RAM_part #(.addrWidth(10), .dataWidth(32), .bus("separate"), .Select("low")) L2_Data_RAM_5 (
    .addr(in_2[14:5]), .din(in_12), .data(L2_DataOut_5_31__0), .str(in_5), .sel(1'b0), .clk(in_1), .ld(1'b1),
    .clr(in_6));
  RAM_part #(.addrWidth(10), .dataWidth(32), .bus("separate"), .Select("low")) L2_Data_RAM_6 (
    .addr(in_2[14:5]), .din(in_13), .data(L2_DataOut_6_31__0), .str(in_5), .sel(1'b0), .clk(in_1), .ld(1'b1),
    .clr(in_6));
  RAM_part #(.addrWidth(10), .dataWidth(32), .bus("separate"), .Select("low")) L2_Data_RAM_7 (
    .addr(in_2[14:5]), .din(in_14), .data(L2_DataOut_7_31__0), .str(in_5), .sel(1'b0), .clk(in_1), .ld(1'b1),
    .clr(in_6));

  // Other names for the same wires on the sheet: clk = in_1; L2_DataIn_0_31__0[31:0] = in_7;
  //   L2_DataIn_1_31__0[31:0] = in_8; L2_DataIn_2_31__0[31:0] = in_9; L2_DataIn_3_31__0[31:0] = in_10;
  //   L2_DataIn_4_31__0[31:0] = in_11; L2_DataIn_5_31__0[31:0] = in_12; L2_DataIn_6_31__0[31:0] = in_13;
  //   L2_DataIn_7_31__0[31:0] = in_14; L2_LoadLine = in_6; L2_WriteData = in_5; L2_WriteTag = in_3;
  //   L2_WriteValid = in_4

  // Notes on the sheet:
  //   L2_Offset
  //   L2_Index
  //   L2_Tag
  //   L2_Tag
  //   L2_StoredTag
  //   L2_TagMatch
  //   L2_Valid
  //   L2_Hit
  //   L2_Miss
endmodule
