// Logisim project cpu4bits.circ as structural Verilog: 1 circuit, main circuit main
module main (
  input  in_1
);

  wire clock, decoder_1_out0, decoder_1_out1, decoder_1_out2, r1, r2;
  wire [3:0] demultiplexer_1_out0, demultiplexer_1_out1, inm, multiplexer_1_out;
  wire [7:0] PC_q, rom_1_data;
  wire [7:6] IR_q;

  Counter PC (.Q(PC_q), .clk(clock));  // open: load, D, count, carry, clr, preset, down
  Clock clock_1 (.out(clock));
  ROM #(.Select("low")) rom_1 (.addr(PC_q), .data(rom_1_data));
  Register #(.Select("low")) IR (.D(rom_1_data), .Q({IR_q, r1, r2, inm}), .clk(clock));  // open: en, clr
  Decoder #(.select(2), .enable("false")) decoder_1 (
    .out0(decoder_1_out0), .out1(decoder_1_out1), .out2(decoder_1_out2), .sel(IR_q));  // open: out3
  Register #(.width(1), .Select("low")) register_1 (.D(decoder_1_out0), .clk(clock));  // open: en, Q, clr
  Register #(.width(1), .Select("low")) register_2 (
    .D(decoder_1_out1), .en(decoder_1_out1), .clk(clock));  // open: Q, clr
  Multiplexer #(.width(4)) multiplexer_1 (
    .in0(inm), .out(multiplexer_1_out), .sel(in_1), .en(decoder_1_out2));  // open: in1
  Demultiplexer #(.width(4), .enable("false")) demultiplexer_1 (
    .out0(demultiplexer_1_out0), .out1(demultiplexer_1_out1), .in(multiplexer_1_out), .sel(r1));
  Register #(.width(4), .Select("low")) RA (.D(demultiplexer_1_out0), .clk(clock));  // open: en, Q, clr
  Register #(.width(4), .Select("low")) RB (.D(demultiplexer_1_out1), .clk(clock));  // open: en, Q, clr

  // Notes on the sheet:
  //   loadi  |  RA   |       |  10$  10    |  0     |  0   | 1010 = 8A
  //   loadi  |  RB   |        |  2$  10    |  1      |  0   | 0010 = A2
  //   contents of rom_1 (hex, n*v repeats v):
  //   a2 8a
endmodule
